// Logisim project 0.System.circ as structural Verilog: 3 circuits, main circuit RAM
module sys (
  input  in_1
);

  wire clk, cpu_1_bus_write, cpu_1_out_7;
  wire [7:0] cpu_1_addr, cpu_1_bus_out;
  wire [31:0] cpu_1_out_8;

  Clock clock_1 (.out(clk));
  cpu cpu_1 (
    .bus_in(cpu_1_bus_out), .bus_out(cpu_1_bus_out), .addr(cpu_1_addr), .bus_write(cpu_1_bus_write),
    .clk(clk), .rst(in_1), .out_7(cpu_1_out_7), .out_8(cpu_1_out_8));
  // Probe on cpu_1_out_8[7:0]
  // Probe on cpu_1_out_8[15:8]
  // Probe on cpu_1_out_8[23:16]
  // Probe on cpu_1_out_8[31:24]
  // Probe on cpu_1_addr
  // Probe on cpu_1_bus_out
  // Probe on cpu_1_bus_write
  RAM ram_1 (
    .data_in(cpu_1_bus_out), .clk(clk), .rst(in_1), .data_out(cpu_1_bus_out), .addr(cpu_1_addr),
    .write(cpu_1_bus_write));
  ROM rom_1 (.addr(cpu_1_addr), .data_out(cpu_1_bus_out));
  GPIO gpio_1 (
    .clk(clk), .rst(in_1), .data_in(cpu_1_bus_out), .addr(cpu_1_addr), .write(cpu_1_bus_write));  // open: data_out, p0, p4, p1, p5, p2, p6, p3, p7

  // Other names for the same wires on the sheet: rst = in_1

  // Notes on the sheet:
  //   End = 0x7F
  //   Start = 0x00
  //   End = 0xBF
  //   Start = 0x80
  //   End = 0xC3
  //   Start = 0xC0
endmodule

module RAM (
  input  [7:0] addr,
  input  [7:0] data_in,
  input  clk,
  input  rst,
  input  write,
  output [7:0] data_out
);

  wire and_1_out, wr_n;
  wire [7:0] ram_1_data;

  not not_1 (wr_n, write);
  and and_1 (and_1_out, ~addr[6], addr[7]);  // AND_Gate
  RAM_part #(.addrWidth(6)) ram_1 (
    .addr(addr[5:0]), .data(ram_1_data), .sel(and_1_out), .clk(clk), .ld(wr_n), .clr(rst));
  assign data_out = wr_n ? ram_1_data : 8'bz;  // Controlled_Buffer controlled_buffer_1
  assign ram_1_data = write ? data_in : 8'bz;  // Controlled_Buffer controlled_buffer_2

  // Other names for the same wires on the sheet: wr = write
endmodule

module ROM (
  input  [7:0] addr,
  output [7:0] data_out
);

  wire not_1_out;
  wire [7:0] rom_1_data;

  not not_1 (not_1_out, addr[7]);
  ROM_part #(.addrWidth(7)) rom_1 (.addr(addr[6:0]), .data(rom_1_data), .sel(not_1_out));
  assign data_out = not_1_out ? rom_1_data : 8'bz;  // Controlled_Buffer controlled_buffer_1

  // Notes on the sheet:
  //   contents of rom_1 (hex, n*v repeats v):
  //   d0 0 d1 0 d2 4 d3 3 8 fc d ff f 11 1 13 ff fe 8 d3 80 a3 13 1 a7 13 ff 8d 50 ff 10 1 1 fd 25 ff 23
  //   ff 25 10*0 9
endmodule
