// Logisim project 1.uFe8.circ as structural Verilog: 5 circuits, main circuit cpu
module cpu (
  input  clk,
  input  rst,
  input  [7:0] bus_in,
  output bus_write,
  output [7:0] bus_out,
  output [7:0] addr,
  output out_7,
  output [31:0] out_8
);

  wire ctrl_1_a_sel, ctrl_1_reg_wr, fetch_cte, fetch_instr, or_1_out, pc_ld;
  wire [1:0] bus_addr_sel, ctrl_1_op, ctrl_1_r_in_sel, ctrl_1_s1, ctrl_1_s2, ula_1_flags;
  wire [7:0] cte, dst, instr, multiplexer_1_out, PC, regs_1_o1, res, src;

  ctrl ctrl_1 (
    .clk(clk), .rst(rst), .r_in_sel(ctrl_1_r_in_sel), .reg_wr(ctrl_1_reg_wr), .s2(ctrl_1_s2), .op(ctrl_1_op),
    .bus_write(bus_write), .flags(ula_1_flags), .instr(instr), .s1(ctrl_1_s1), .A_sel(ctrl_1_a_sel),
    .pc_ld(pc_ld), .fetch_instr(fetch_instr), .fetch_cte(fetch_cte), .bus_addr_sel(bus_addr_sel),
    .dbg_cycle(out_7));
  // Probe on ctrl_1_r_in_sel
  Multiplexer #(.select(2), .width(8), .disabled(0), .enable("false")) multiplexer_1 (
    .in0(res), .in1(bus_in), .in2(src), .in3(src), .out(multiplexer_1_out), .sel(ctrl_1_r_in_sel));
  // Probe on multiplexer_1_out
  or or_1 (or_1_out, fetch_instr, fetch_cte);
  Counter u_PC (.load(pc_ld), .D(cte), .count(or_1_out), .Q(PC), .clk(clk), .clr(rst));  // open: carry
  // Probe on ctrl_1_s1
  // Probe on ctrl_1_s2
  // Probe on regs_1_o1
  regs regs_1 (
    .clk(clk), .rst(rst), .s1(ctrl_1_s1), .s2(ctrl_1_s2), .o1(regs_1_o1), .o2(dst), .wr(ctrl_1_reg_wr),
    .di(multiplexer_1_out), .dbg_regs(out_8));
  // Probe on dst
  Multiplexer #(.width(8), .disabled(0), .enable("false")) multiplexer_2 (
    .in0(cte), .in1(regs_1_o1), .out(src), .sel(ctrl_1_a_sel));
  // Probe on src
  Register u_instr (.D(bus_in), .en(fetch_instr), .Q(instr), .clk(clk), .clr(rst));
  // Probe on ctrl_1_op
  // Probe on ula_1_flags
  ula ula_1 (.op(ctrl_1_op), .A(src), .B(dst), .O(res), .flags(ula_1_flags));
  // Probe on res
  Register u_cte (.D(bus_in), .en(fetch_cte), .Q(cte), .clk(clk), .clr(rst));
  assign bus_out = bus_write ? src : 8'bz;  // Controlled_Buffer controlled_buffer_1
  // Probe on bus_addr_sel
  Multiplexer #(.select(2), .width(8), .disabled(0), .enable("false")) multiplexer_3 (
    .in0(PC), .in1(src), .in2(dst), .in3(dst), .out(addr), .sel(bus_addr_sel));

  // Other names for the same wires on the sheet: bus_wr = bus_write; dbg_cycle = out_7; dbg_r[31:0] = out_8

  // Notes on the sheet:
  //   PC
  //   Barramento
endmodule

module ula (
  input  [7:0] A,
  input  [7:0] B,
  input  [1:0] op,
  output [7:0] O,
  output [1:0] flags
);

  wire [7:0] add, \and , \or , \xor ;

  add8 add8_1 (.A(B), .B(A), .co(flags[0]), .S(add), .ci(1'b0));
  assign \and  = A & B;  // AND_Gate and_1, 8 bits wide
  assign \xor  = A ^ B;  // XOR_Gate xor_1, 8 bits wide
  assign \or  = A | B;  // OR_Gate or_1, 8 bits wide
  Multiplexer #(.select(2), .width(8), .disabled(0), .enable("false")) multiplexer_1 (
    .in0(add), .in1(\and ), .in2(\xor ), .in3(\or ), .out(O), .sel(op));
  nor nor_1 (flags[1], O[0], O[1], O[2], O[3], O[4], O[5], O[6], O[7]);

  // Other names for the same wires on the sheet: co = flags[0]; z = flags[1]; out[7:0] = O

  // Notes on the sheet:
  //   Operações aritiméticas
  //   Operações lógicas
  //   flag: zero
endmodule

module regs (
  input  [7:0] di,
  input  [1:0] s1,
  input  [1:0] s2,
  input  clk,
  input  rst,
  input  wr,
  output [7:0] o1,
  output [7:0] o2,
  output [31:0] dbg_regs
);

  wire e0, e1, e2, e3;

  Demultiplexer #(.select(2), .disabled(0), .enable("false")) demultiplexer_1 (
    .out0(e0), .out1(e1), .out2(e2), .out3(e3), .in(wr), .sel(s2));
  Register register_1 (.D(di), .en(e0), .Q(dbg_regs[7:0]), .clk(clk), .clr(rst));
  Register register_2 (.D(di), .en(e2), .Q(dbg_regs[23:16]), .clk(clk), .clr(rst));
  Register register_3 (.D(di), .en(e1), .Q(dbg_regs[15:8]), .clk(clk), .clr(rst));
  Register register_4 (.D(di), .en(e3), .Q(dbg_regs[31:24]), .clk(clk), .clr(rst));
  Multiplexer #(.select(2), .width(8), .disabled(0), .enable("false")) multiplexer_1 (
    .in0(dbg_regs[7:0]), .in1(dbg_regs[15:8]), .in2(dbg_regs[23:16]), .in3(dbg_regs[31:24]), .out(o1),
    .sel(s1));
  Multiplexer #(.select(2), .width(8), .disabled(0), .enable("false")) multiplexer_2 (
    .in0(dbg_regs[7:0]), .in1(dbg_regs[15:8]), .in2(dbg_regs[23:16]), .in3(dbg_regs[31:24]), .out(o2),
    .sel(s2));

  // Other names for the same wires on the sheet: r0[7:0] = dbg_regs[7:0]; r1[7:0] = dbg_regs[15:8];
  //   r2[7:0] = dbg_regs[23:16]; r3[7:0] = dbg_regs[31:24]

  // Notes on the sheet:
  //   Habilitador de escrita
endmodule

module ctrl (
  input  clk,
  input  rst,
  input  [1:0] flags,
  input  [7:0] instr,
  output dbg_cycle,
  output A_sel,
  output reg_wr,
  output bus_write,
  output fetch_instr,
  output fetch_cte,
  output pc_ld,
  output [1:0] s1,
  output [1:0] s2,
  output [1:0] op,
  output [1:0] bus_addr_sel,
  output [1:0] r_in_sel
);

  wire and_1_out, and_2_out, and_3_out, and_4_out, ci, cond_met, decode, exec, Jumps, LD, not_1_out,
       or_1_out, or_2_out, or_3_out, ST, z;
  wire [1:0] multiplexer_2_out, multiplexer_3_out;

  and and_1 (and_1_out, exec, ~instr[7]);  // AND_Gate
  Register #(.width(2)) u_flags (.D(flags), .en(and_1_out), .Q({z, ci}), .clk(clk), .clr(rst));
  Decoder #(.select(3), .disabled(0), .enable("false")) decoder_1 (
    .out4(LD), .out5(ST), .out7(Jumps), .sel(instr[7:5]));  // open: out0, out1, out2, out3, out6
  and and_2 (and_2_out, decode, ~instr[4]);  // AND_Gate
  Multiplexer #(.select(2), .disabled(0), .enable("false")) multiplexer_1 (
    .in0(ci), .in1(z), .in2(not_1_out), .in3(1'b1), .out(cond_met), .sel(instr[1:0]));
  not not_1 (not_1_out, z);
  and and_3 (and_3_out, decode, instr[4]);
  or or_1 (or_1_out, and_2_out, fetch_cte);
  D_Flip_Flop d_ff_1 (.clk(clk), .D(dbg_cycle), .Q(fetch_instr), .preset(rst));  // open: Qn, en, reset
  D_Flip_Flop d_ff_2 (.clk(clk), .D(fetch_instr), .Q(decode), .reset(rst));  // open: Qn, preset, en
  D_Flip_Flop d_ff_3 (.clk(clk), .D(and_3_out), .Q(fetch_cte), .reset(rst));  // open: Qn, preset, en
  D_Flip_Flop d_ff_4 (.clk(clk), .D(or_1_out), .Q(exec), .reset(rst));  // open: Qn, preset, en
  D_Flip_Flop d_ff_5 (.clk(clk), .D(exec), .Q(dbg_cycle), .reset(rst));  // open: Qn, preset, en
  and and_4 (and_4_out, dbg_cycle, or_2_out);
  or or_2 (or_2_out, LD, ST);
  Multiplexer #(.width(2), .disabled(0), .enable("false")) multiplexer_2 (
    .in0(2'b01), .in1(2'b10), .out(multiplexer_2_out), .sel(instr[5]));
  Multiplexer #(.width(2), .disabled(0), .enable("false")) multiplexer_3 (
    .in0(2'b01), .in1(2'b10), .out(multiplexer_3_out), .sel(instr[6]));
  or or_3 (or_3_out, ~instr[5], ~instr[7]);  // OR_Gate
  and and_5 (reg_wr, or_3_out, dbg_cycle);
  and and_6 (bus_write, ST, dbg_cycle);
  and and_7 (pc_ld, Jumps, dbg_cycle, cond_met);
  Multiplexer #(.width(2), .disabled(0), .enable("false")) multiplexer_4 (
    .in0(2'b00), .in1(multiplexer_2_out), .out(bus_addr_sel), .sel(and_4_out));
  Multiplexer #(.width(2), .disabled(0), .enable("false")) multiplexer_5 (
    .in0(2'b00), .in1(multiplexer_3_out), .out(r_in_sel), .sel(instr[7]));
  not not_2 (A_sel, instr[4]);

  assign op = instr[6:5];
  assign s1 = instr[3:2];
  assign s2 = instr[1:0];

  // Other names for the same wires on the sheet: cond[1:0] = instr[1:0]; dst[1:0] = instr[1:0]; fetch = fetch_instr;
  //   cte = instr[4]; op_0 = instr[5]; op_t[2:0] = instr[7:5]; op_1 = instr[6]; op_2 = instr[7];
  //   src[1:0] = instr[3:2]; write = dbg_cycle

  // Notes on the sheet:
  //   v n z c
  //   src
  //   dst
  //   bus
  //   src
  //   PC
  //   res
endmodule

module cpu_tb (
  input  in_1
);

  wire clock_1_out, cpu_1_out_7, wr;
  wire [7:0] addr, data;
  wire [31:0] cpu_1_out_8;

  Clock clock_1 (.out(clock_1_out));
  cpu cpu_1 (
    .bus_in(data), .bus_out(data), .addr(addr), .bus_write(wr), .clk(clock_1_out), .rst(in_1),
    .out_7(cpu_1_out_7), .out_8(cpu_1_out_8));
  // Probe on cpu_1_out_8[7:0]
  // Probe on cpu_1_out_8[15:8]
  // Probe on cpu_1_out_8[23:16]
  // Probe on cpu_1_out_8[31:24]
  // Probe on data
  // Probe on addr
  ROM rom_1 (.addr(addr), .data(data));  // open: sel

  // Notes on the sheet:
  //   R0
  //   R1
  //   R2
  //   R3
  //   contents of rom_1 (hex, n*v repeats v):
  //   d0 0 d1 0 d2 4 d3 3 8 fc d ff f 11 1 13 ff fe 8 ff 13
endmodule
