// Logisim project 2.GPIO.circ as structural Verilog: 2 circuits, main circuit GPIO
module GPIO (
  input  clk,
  input  rst,
  input  [7:0] data_in,
  input  [7:0] addr,
  input  write,
  output [7:0] data_out,
  output p0,
  output p4,
  output p1,
  output p5,
  output p2,
  output p6,
  output p3,
  output p7
);

  wire and_1_out, dir_en, gpio_en, out_en, ren_en;
  wire [7:0] dir, inp, out, ren;

  Register u_dir (.D(data_in), .en(dir_en), .Q(dir), .clk(clk), .clr(rst));
  Register u_out (.D(data_in), .en(out_en), .Q(out), .clk(clk), .clr(rst));
  Comparator #(.width(4)) comparator_1 (.a(addr[7:4]), .b(4'b0000), .eq(gpio_en));  // open: gt, lt
  Demultiplexer #(.select(2), .disabled(0)) demultiplexer_1 (
    .out0(dir_en), .out1(ren_en), .out2(out_en), .in(write), .sel(addr[1:0]), .en(gpio_en));  // open: out3
  Register u_ren (.D(data_in), .en(ren_en), .Q(ren), .clk(clk), .clr(rst));
  Multiplexer #(.select(2), .width(8)) multiplexer_1 (
    .in0(dir), .in1(ren), .in2(out), .in3(inp), .out(data_out), .sel(addr[1:0]), .en(and_1_out));
  and and_1 (and_1_out, ~write, gpio_en);  // AND_Gate
  pad pad_1 (.ren(ren[0]), .out(out[0]), .dir(dir[0]), .in(inp[0]), .pad_2(p0));  // open: pad
  pad pad_2 (.ren(ren[1]), .out(out[1]), .dir(dir[1]), .in(inp[1]), .pad_2(p1));  // open: pad
  pad pad_3 (.ren(ren[2]), .out(out[2]), .dir(dir[2]), .in(inp[2]), .pad_2(p2));  // open: pad
  pad pad_4 (.ren(ren[3]), .out(out[3]), .dir(dir[3]), .in(inp[3]), .pad_2(p3));  // open: pad
  pad pad_5 (.ren(ren[4]), .out(out[4]), .dir(dir[4]), .in(inp[4]), .pad_2(p4));  // open: pad
  pad pad_6 (.ren(ren[5]), .out(out[5]), .dir(dir[5]), .in(inp[5]), .pad_2(p5));  // open: pad
  pad pad_7 (.ren(ren[6]), .out(out[6]), .dir(dir[6]), .in(inp[6]), .pad_2(p6));  // open: pad
  pad pad_8 (.ren(ren[7]), .out(out[7]), .dir(dir[7]), .in(inp[7]), .pad_2(p7));  // open: pad

  // Other names for the same wires on the sheet: reg_sel[1:0] = addr[1:0]; di[7:0] = data_in; dir__0 = dir[0];
  //   dir__1 = dir[1]; dir__2 = dir[2]; dir__3 = dir[3]; dir__4 = dir[4]; dir__5 = dir[5]; dir__6 = dir[6];
  //   dir__7 = dir[7]; do[7:0] = data_out; inp__0 = inp[0]; inp__1 = inp[1]; inp__2 = inp[2]; inp__3 = inp[3];
  //   inp__4 = inp[4]; inp__5 = inp[5]; inp__6 = inp[6]; inp__7 = inp[7]; out__0 = out[0]; out__1 = out[1];
  //   out__2 = out[2]; out__3 = out[3]; out__4 = out[4]; out__5 = out[5]; out__6 = out[6]; out__7 = out[7];
  //   ren__0 = ren[0]; ren__1 = ren[1]; ren__2 = ren[2]; ren__3 = ren[3]; ren__4 = ren[4]; ren__5 = ren[5];
  //   ren__6 = ren[6]; ren__7 = ren[7]; wr = write

  // Notes on the sheet:
  //   Write Select
  //   Output select
  //   Pinos externos (PADS)
endmodule

module pad (
  input  out,
  input  ren,
  input  dir,
  input  pad,
  output pad_2,
  output in
);

  wire pull_resistor_1_node, pull_resistor_2_node;

  Pull_Resistor pull_resistor_1 (.node(pull_resistor_1_node));
  assign pad = dir ? out : 1'bz;  // Controlled_Buffer controlled_buffer_1
  buf buffer_1 (in, pad);
  Pull_Resistor #(.pull(1)) pull_resistor_2 (.node(pull_resistor_2_node));
  Multiplexer multiplexer_1 (.in0(pull_resistor_1_node), .in1(pull_resistor_2_node), .out(pad), .sel(out), .en(ren));

  assign pad_2 = pad;
endmodule
