// Logisim project 3.Math.circ as structural Verilog: 5 circuits, main circuit fa
module fa (
  input  a,
  input  b,
  input  ci,
  output co,
  output s
);

  wire and_1_out, and_2_out, and_3_out, and_4_out, and_5_out, and_6_out, and_7_out;

  and and_1 (and_1_out, a, b);
  and and_2 (and_2_out, a, ci);
  and and_3 (and_3_out, b, ci);
  and and_4 (and_4_out, ~a, ~b, ci);  // AND_Gate
  and and_5 (and_5_out, a, ~b, ~ci);  // AND_Gate
  and and_6 (and_6_out, ~a, b, ~ci);  // AND_Gate
  and and_7 (and_7_out, a, b, ci);
  or or_1 (co, and_1_out, and_2_out, and_3_out);
  or or_2 (s, and_4_out, and_5_out, and_6_out, and_7_out);
endmodule

module add4 (
  input  [3:0] A,
  input  [3:0] B,
  input  ci,
  output [3:0] A_2,
  output co
);

  wire fa_2_co, fa_3_co, fa_4_co;

  fa fa_1 (.a(A[3]), .b(B[3]), .ci(fa_2_co), .co(co), .s(A_2[3]));
  fa fa_2 (.a(A[2]), .b(B[2]), .ci(fa_3_co), .co(fa_2_co), .s(A_2[2]));
  fa fa_3 (.a(A[1]), .b(B[1]), .ci(fa_4_co), .co(fa_3_co), .s(A_2[1]));
  fa fa_4 (.a(A[0]), .b(B[0]), .ci(ci), .co(fa_4_co), .s(A_2[0]));

  // Other names for the same wires on the sheet: s0 = A_2[0]; s1 = A_2[1]; s2 = A_2[2]; s3 = A_2[3]
endmodule

module add8 (
  input  [7:0] A,
  input  [7:0] B,
  input  ci,
  output [7:0] S,
  output co
);

  wire add4_2_co;

  add4 add4_1 (.A(B[7:4]), .B(A[7:4]), .ci(add4_2_co), .A_2(S[7:4]), .co(co));
  add4 add4_2 (.A(B[3:0]), .B(A[3:0]), .ci(ci), .A_2(S[3:0]), .co(add4_2_co));

  // Other names for the same wires on the sheet: A_L[3:0] = A[3:0]; A_H[3:0] = A[7:4]; B_L[3:0] = B[3:0];
  //   B_H[3:0] = B[7:4]; S_L[3:0] = S[3:0]; S_H[3:0] = S[7:4]
endmodule

module mult4 (
  input  [3:0] A,
  input  [3:0] B,
  output [7:0] P
);

  wire fa_2_co, fa_2_s, fa_3_co, fa_4_co, fa_4_s, fa_5_co, fa_5_s, fa_6_co, fa_7_co, fa_7_s, fa_8_co, fa_8_s,
       fa_9_co, fa_10_co, fa_10_s, fa_11_co, fa_12_co, p01, p02, p03, p10, p11, p12, p13, p20, p21, p22, p23,
       p30, p31, p32, p33;

  fa fa_1 (.a(fa_2_co), .b(p33), .ci(fa_3_co), .co(P[7]), .s(P[6]));
  fa fa_2 (.a(fa_4_co), .b(p23), .ci(fa_5_co), .co(fa_2_co), .s(fa_2_s));
  fa fa_3 (.a(fa_2_s), .b(p32), .ci(fa_6_co), .co(fa_3_co), .s(P[5]));
  and and_1 (p03, A[0], B[3]);
  and and_2 (p13, A[1], B[3]);
  and and_3 (p23, A[2], B[3]);
  and and_4 (p33, A[3], B[3]);
  fa fa_4 (.a(p13), .b(1'b0), .ci(fa_7_co), .co(fa_4_co), .s(fa_4_s));
  fa fa_5 (.a(fa_4_s), .b(p22), .ci(fa_8_co), .co(fa_5_co), .s(fa_5_s));
  fa fa_6 (.a(fa_5_s), .b(p31), .ci(fa_9_co), .co(fa_6_co), .s(P[4]));
  fa fa_7 (.a(p12), .b(p03), .ci(fa_10_co), .co(fa_7_co), .s(fa_7_s));
  fa fa_8 (.a(fa_7_s), .b(p21), .ci(fa_11_co), .co(fa_8_co), .s(fa_8_s));
  fa fa_9 (.a(fa_8_s), .b(p30), .ci(1'b0), .co(fa_9_co), .s(P[3]));
  and and_5 (p02, A[0], B[2]);
  and and_6 (p12, A[1], B[2]);
  and and_7 (p22, A[2], B[2]);
  and and_8 (p32, A[3], B[2]);
  and and_9 (p01, A[0], B[1]);
  and and_10 (p11, A[1], B[1]);
  and and_11 (p21, A[2], B[1]);
  and and_12 (p31, A[3], B[1]);
  fa fa_10 (.a(p11), .b(p02), .ci(fa_12_co), .co(fa_10_co), .s(fa_10_s));
  fa fa_11 (.a(fa_10_s), .b(p20), .ci(1'b0), .co(fa_11_co), .s(P[2]));
  fa fa_12 (.a(p10), .b(p01), .ci(1'b0), .co(fa_12_co), .s(P[1]));
  and and_13 (P[0], A[0], B[0]);
  and and_14 (p10, A[1], B[0]);
  and and_15 (p20, A[2], B[0]);
  and and_16 (p30, A[3], B[0]);

  // Other names for the same wires on the sheet: p00 = P[0]
endmodule

module mult8 (
  input  [7:0] A,
  input  [7:0] B,
  output [15:0] R
);

  wire add4_3_co, add4_4_co, add4_5_co;
  wire [0:0] add4_2_co;
  wire [3:0] add4_2_a_2, add4_4_a_2, P0H, P1H, P1L, P2H, P2L, P3H, P3L;

  add4 add4_1 (.A(P3H), .B({3'b000, add4_2_co[0]}), .ci(add4_3_co), .A_2(R[15:12]));  // open: co
  add4 add4_2 (.A(P2H), .B(P1H), .ci(add4_4_co), .A_2(add4_2_a_2), .co(add4_2_co[0]));
  add4 add4_3 (.A(add4_2_a_2), .B(P3L), .ci(add4_5_co), .A_2(R[11:8]), .co(add4_3_co));
  mult4 mult4_1 (.A(B[7:4]), .B(A[7:4]), .P({P3H, P3L}));
  add4 add4_4 (.A(P1L), .B(P0H), .ci(1'b0), .A_2(add4_4_a_2), .co(add4_4_co));
  add4 add4_5 (.A(add4_4_a_2), .B(P2L), .ci(1'b0), .A_2(R[7:4]), .co(add4_5_co));
  mult4 mult4_2 (.A(B[3:0]), .B(A[7:4]), .P({P2H, P2L}));
  mult4 mult4_3 (.A(B[7:4]), .B(A[3:0]), .P({P1H, P1L}));
  mult4 mult4_4 (.A(B[3:0]), .B(A[3:0]), .P({P0H, R[3:0]}));

  // Other names for the same wires on the sheet: AL[3:0] = A[3:0]; AH[3:0] = A[7:4]; BL[3:0] = B[3:0];
  //   BH[3:0] = B[7:4]; P0L[3:0] = R[3:0]; R0[3:0] = R[3:0]; R1[3:0] = R[7:4]; R2[3:0] = R[11:8]; R3[3:0] = R[15:12]
endmodule
